# Fritzing sketch control_light_by_phonefzz (saved by Fritzing 0.9.3b)
breadboards: 1

parts:
  Part1 = Arduino Nano (Rev3.0)
  Part2 = Bluetooth HC-05 Macho
  R1 = Resistor [tolerance=±5% resistance=2k package="1206 [SMD]"]
  R2 = Resistor [tolerance=±5% resistance=1k package="1206 [SMD]"]
  U1 = 2-Channel 5v Relay Shield [package=relay-2ch5v10a]
  LED1 = LEDs [package=led10mm]
  LED2 = LEDs [package=led10mm]
  JP1 = Header 2 [package=jst-2-smd]

nets:
  GND: Part1.GND, Part2.GND, R1.Pin_0, U1.GND
  N1: Part1.D2, U1.IN2
  N2: Part1.D3, U1.IN1
  N3: Part1.D4, Part2.TXD
  N4: Part1.D5, R2.Pin_0
  VCC: Part1.VIN, Part2.VCC, U1.VCC
  N5: Part2.RXD, R1.Pin_1, R2.Pin_1
  N6: U1.K1-In, LED1.A
  N7: U1.K1-On, U1.K2-In, JP1.2
  N8: U1.K2-On, LED2.C
  N9: LED1.C, LED2.A, JP1.1

notes:
  220V AC

custom parts:
  2-Channel 5v Relay Shield: 2 Channel 5v Relay Shield w. 2x SPD-06VDC-SD-C
  LEDs: LEDs Standard schematic elements and footprints for 5mm, 3mm, 1206, and 0603 sized LEDs. 5mm - Spark Fun Electronics SKU : COM-00529 (and others)
